// Digital circuit singlecycle.dig as structural Verilog
module singlecycle (
  input  clk,
  input  [31:0] d_rdat,
  input  en,
  input  [31:0] instr,
  input  ack,
  output [31:0] d_adr,
  output [31:0] pc,
  output [31:0] d_wdat,
  output [3:0] d_msk,
  output [30:0] test,
  output [4:0] uop,
  output busy,
  output pass,
  output fail
);

  wire add_2_c_o, alt, and_5_out, comparator_2_eq, comparator_3_eq, comparator_5_eq, comparator_6_eq, en_ir,
       en_mar, en_pc, en_reg, en_str, J, LN, lt, ltu, multiplexer_1_out, multiplexer_22_out, mux_ack,
       mux_func, mux_lhs, mux_pc, mux_rhs, mux_sb, mux_sub, N, next, not_3_out, not_4_out, not_5_out,
       rd_zero, register_1_q, RN, rs, sub, V, Z;
  wire [0:0] multiplexer_2_out, register_3_q;
  wire [1:0] bitextender_6_out, demultiplexer_4_out_0, demultiplexer_4_out_1, mux_br, mux_imm, mux_res;
  wire [2:0] funct3, multiplexer_16_out;
  wire [3:0] bitextender_7_out, demultiplexer_3_out_0, multiplexer_2_out_2;
  wire [4:0] rd, rs1, rs2, uop_mapper_wrapper_1_uop;
  wire [6:0] funct7, ir_q;
  wire [7:0] dat0_d, dat1_d, dat2_d, dat3_d, demultiplexer_1_out_0, demultiplexer_1_out_1,
       demultiplexer_1_out_2, demultiplexer_1_out_3, multiplexer_3_out;
  wire [8:8] multiplexer_6_out;
  wire [15:0] multiplexer_4_out;
  wire [16:16] multiplexer_7_out;
  wire [30:0] add_2_s, multiplexer_9_out, multiplexer_13_out;
  wire [31:0] add_1_s, and_2_out, bitextender_1_out, bitextender_2_out, bitextender_3_out, bitextender_4_out,
       bitextender_5_out, demultiplexer_2_out_0, multiplexer_5_out, multiplexer_10_out, multiplexer_11_out,
       multiplexer_12_out, multiplexer_15_out, not_1_out, or_1_out, or_2_out, or_3_out, prog_d, res_t, rf_da,
       rf_db, sll_out, srl_a_out, xor_1_out;
  wire [31:1] ucode_d;
  wire [32:32] srl_a_out_2;

  ROM #(.AddrBits(16), .isProgramMemory("true"), .Bits(32)) prog (.A(pc[17:2]), .sel(1'b1), .D(prog_d));
  assign or_1_out = d_rdat | {dat3_d, dat2_d, dat1_d, dat0_d};  // Or or_1, 32 bits wide
  assign or_2_out = instr | prog_d;  // Or or_2, 32 bits wide
  Multiplexer multiplexer_1 (.sel(mux_ack), .in_0(next), .in_1(ack), .out(multiplexer_1_out));
  Comparator #(.Bits(5)) comparator_1 (.a(rd), .b({5{1'b0}}), .eq(rd_zero));  // open: gt, lt
  Multiplexer #(.Bits(5)) multiplexer_2 (
    .sel(mux_sb), .in_0(rs2), .in_1(rd), .out({multiplexer_2_out_2, multiplexer_2_out[0]}));
  Register #(.Bits(32)) ir (
    .D(or_2_out), .C(clk), .en(en_ir), .Q({funct7[6], alt, funct7[4:0], rs2, rs1, funct3, rd, ir_q}));
  Add #(.Bits(32)) add_1 (.a(pc), .b(32'h4), .c_i(1'b0), .s(add_1_s));  // open: c_o
  Comparator comparator_2 (.a(LN), .b(RN), .eq(comparator_2_eq));  // open: gt, lt
  Multiplexer #(.Selector_Bits(2), .Bits(8)) multiplexer_3 (
    .sel(d_adr[1:0]), .in_0(or_1_out[7:0]), .in_1(or_1_out[15:8]), .in_2(or_1_out[23:16]),
    .in_3(or_1_out[31:24]), .out(multiplexer_3_out));
  Multiplexer #(.Bits(16)) multiplexer_4 (
    .sel(d_adr[1]), .in_0(or_1_out[15:0]), .in_1(or_1_out[31:16]), .out(multiplexer_4_out));
  uop_mapper_wrapper uop_mapper_wrapper_1 (
    .inst({funct7[6], alt, funct7[4:0], rs2, rs1, funct3, rd, ir_q}), .ack(multiplexer_1_out),
    .uop(uop_mapper_wrapper_1_uop));
  Register register_1 (.D(mux_pc), .C(clk), .en(en), .Q(register_1_q));
  Multiplexer #(.Bits(32)) multiplexer_5 (.sel(mux_pc), .in_0(add_1_s), .in_1({N, add_2_s}), .out(multiplexer_5_out));
  RegisterFile #(.AddrBits(5), .Bits(32)) rf (
    .Din(res_t), .we(en_reg), .Rw(rd), .C(clk), .Ra(rs1), .Rb(rs2), .Da(rf_da), .Db(rf_db));
  BitExtender #(.inputBits(12), .outputBits(32)) bitextender_1 (
    .in({funct7[6], alt, funct7[4:0], multiplexer_2_out_2, multiplexer_2_out[0]}), .out(bitextender_1_out));
  BitExtender #(.inputBits(13), .outputBits(32)) bitextender_2 (
    .in({funct7[6], multiplexer_2_out[0], alt, funct7[4:0], multiplexer_2_out_2, 1'b0}),
    .out(bitextender_2_out));
  BitExtender #(.inputBits(21), .outputBits(32)) bitextender_3 (
    .in({funct7[6], rs1, funct3, multiplexer_2_out[0], alt, funct7[4:0], multiplexer_2_out_2, 1'b0}),
    .out(bitextender_3_out));
  Comparator comparator_3 (.a(LN), .b(N), .eq(comparator_3_eq));  // open: gt, lt
  Multiplexer multiplexer_6 (.sel(funct3[2]), .in_0(multiplexer_3_out[7]), .in_1(1'b0), .out(multiplexer_6_out[8]));
  Multiplexer multiplexer_7 (.sel(funct3[2]), .in_0(multiplexer_4_out[15]), .in_1(1'b0), .out(multiplexer_7_out[16]));
  Multiplexer #(.Bits(5)) multiplexer_8 (
    .sel(register_1_q), .in_0(uop_mapper_wrapper_1_uop), .in_1({5{1'b0}}), .out(uop));
  Register #(.Bits(32)) u_pc (.D(multiplexer_5_out), .C(clk), .en(en_pc), .Q(pc));
  and and_1 (V, comparator_2_eq, ~comparator_3_eq);  // And
  BitExtender #(.inputBits(9), .outputBits(32)) bitextender_4 (
    .in({multiplexer_6_out[8], multiplexer_3_out}), .out(bitextender_4_out));
  BitExtender #(.inputBits(17), .outputBits(32)) bitextender_5 (
    .in({multiplexer_7_out[16], multiplexer_4_out}), .out(bitextender_5_out));
  Register register_2 (.D(busy), .C(clk), .en(en), .Q(next));
  Multiplexer #(.Bits(32)) multiplexer_9 (.sel(mux_lhs), .in_0(pc), .in_1(rf_da), .out({LN, multiplexer_9_out}));
  Multiplexer #(.Bits(32)) multiplexer_10 (
    .sel(mux_rhs), .in_0(rf_db), .in_1(multiplexer_11_out), .out(multiplexer_10_out));
  Multiplexer #(.Selector_Bits(2), .Bits(32)) multiplexer_11 (
    .sel(mux_imm), .in_0(bitextender_1_out),
    .in_1({funct7[6], alt, funct7[4:0], multiplexer_2_out_2, multiplexer_2_out[0], rs1, funct3, {12{1'b0}}}),
    .in_2(bitextender_2_out), .in_3(bitextender_3_out), .out(multiplexer_11_out));
  Multiplexer #(.Selector_Bits(2), .Bits(32)) multiplexer_12 (
    .sel(funct3[1:0]), .in_0(bitextender_4_out), .in_1(bitextender_5_out), .in_2(or_1_out), .in_3(or_1_out),
    .out(multiplexer_12_out));
  ROM #(.AddrBits(5), .Bits(32)) ucode (
    .A(uop), .sel(1'b1),
    .D({ucode_d[31:24], mux_res, mux_imm, mux_br, mux_sb, mux_sub, mux_ack, mux_func, mux_rhs, mux_lhs, ucode_d[11:1], busy}));
  Multiplexer #(.Bits(32)) multiplexer_13 (
    .sel(sub), .in_0(multiplexer_10_out), .in_1(not_1_out), .out({RN, multiplexer_13_out}));
  assign not_1_out = ~multiplexer_10_out;  // Not not_1, 32 bits wide
  BarrelShifter #(.Bits(32)) sll (.in({LN, multiplexer_9_out}), .shift(multiplexer_10_out[5:0]), .out(sll_out));
  assign xor_1_out = multiplexer_10_out ^ {LN, multiplexer_9_out};  // XOr xor_1, 32 bits wide
  BarrelShifter #(.Bits(33), .barrelShifterMode("arithmetic")) srl_a (
    .in({rs, LN, multiplexer_9_out}), .shift(multiplexer_10_out[5:0]), .out({srl_a_out_2[32], srl_a_out}));
  assign or_3_out = multiplexer_10_out | {LN, multiplexer_9_out};  // Or or_3, 32 bits wide
  assign and_2_out = multiplexer_10_out & {LN, multiplexer_9_out};  // And and_2, 32 bits wide
  Demultiplexer #(.Selector_Bits(2), .Bits(8)) demultiplexer_1 (
    .sel(d_adr[1:0]), .in(rf_db[7:0]), .out_0(demultiplexer_1_out_0), .out_1(demultiplexer_1_out_1),
    .out_2(demultiplexer_1_out_2), .out_3(demultiplexer_1_out_3));
  Demultiplexer #(.Bits(16)) demultiplexer_2 (
    .sel(d_adr[1]), .in(rf_db[15:0]), .out_0(demultiplexer_2_out_0[15:0]),
    .out_1(demultiplexer_2_out_0[31:16]));
  Add #(.Bits(32)) add_2 (
    .a({LN, multiplexer_9_out}), .b({RN, multiplexer_13_out}), .c_i(sub), .s({N, add_2_s}), .c_o(add_2_c_o));
  Comparator #(.Bits(32)) comparator_4 (.a({N, add_2_s}), .b({32{1'b0}}), .eq(Z));  // open: gt, lt
  not not_2 (ltu, add_2_c_o);
  Multiplexer #(.Selector_Bits(2), .Bits(32)) multiplexer_14 (
    .sel(funct3[1:0]),
    .in_0({demultiplexer_1_out_3, demultiplexer_1_out_2, demultiplexer_1_out_1, demultiplexer_1_out_0}),
    .in_1(demultiplexer_2_out_0), .in_2(rf_db), .in_3(rf_db), .out(d_wdat));
  and and_3 (en_pc, ucode_d[6], en);
  and and_4 (en_reg, ucode_d[7], ~rd_zero, en);  // And
  Multiplexer #(.Selector_Bits(3), .Bits(32)) multiplexer_15 (
    .sel(multiplexer_16_out), .in_0({N, add_2_s}), .in_1(sll_out), .in_2({{31{1'b0}}, lt}),
    .in_3({{31{1'b0}}, ltu}), .in_4(xor_1_out), .in_5(srl_a_out), .in_6(or_3_out), .in_7(and_2_out),
    .out(multiplexer_15_out));
  Multiplexer #(.Bits(3)) multiplexer_16 (.sel(mux_func), .in_0(3'b000), .in_1(funct3), .out(multiplexer_16_out));
  Demultiplexer #(.Selector_Bits(2)) demultiplexer_3 (
    .sel(d_adr[1:0]), .in(en_str), .out_0(demultiplexer_3_out_0[0]), .out_1(demultiplexer_3_out_0[1]),
    .out_2(demultiplexer_3_out_0[2]), .out_3(demultiplexer_3_out_0[3]));
  BitExtender #(.inputBits(1), .outputBits(2)) bitextender_6 (.in(en_str), .out(bitextender_6_out));
  and and_5 (and_5_out, ~rd[0], rd[1], ~rd[2], rd[3], ~rd[4]);  // And
  Register #(.Bits(32)) mar (.D({N, add_2_s}), .C(clk), .en(en_mar), .Q(d_adr));
  Demultiplexer #(.Bits(2)) demultiplexer_4 (
    .sel(d_adr[1]), .in(bitextender_6_out), .out_0(demultiplexer_4_out_0), .out_1(demultiplexer_4_out_1));
  BitExtender #(.inputBits(1), .outputBits(4)) bitextender_7 (.in(en_str), .out(bitextender_7_out));
  Register #(.Bits(32)) register_3 (.D(res_t), .C(clk), .en(and_5_out), .Q({test, register_3_q[0]}));
  Comparator #(.Bits(32)) comparator_5 (
    .a({test, register_3_q[0]}), .b({32{1'b0}}), .eq(comparator_5_eq));  // open: gt, lt
  Comparator #(.Bits(5)) comparator_6 (.a(uop), .b(5'b10010), .eq(comparator_6_eq));  // open: gt, lt
  Multiplexer #(.Selector_Bits(2), .Bits(32)) multiplexer_17 (
    .sel(mux_res), .in_0(add_1_s), .in_1(multiplexer_15_out), .in_2(multiplexer_11_out),
    .in_3(multiplexer_12_out), .out(res_t));
  xor xor_2 (lt, N, V);
  not not_3 (not_3_out, Z);
  not not_4 (not_4_out, lt);
  not not_5 (not_5_out, ltu);
  Multiplexer #(.Selector_Bits(2)) multiplexer_18 (
    .sel(mux_br), .in_0(1'b0), .in_1(1'b1), .in_2(J), .in_3(J), .out(mux_pc));
  Multiplexer #(.Selector_Bits(2), .Bits(4)) multiplexer_19 (
    .sel(funct3[1:0]), .in_0(demultiplexer_3_out_0), .in_1({demultiplexer_4_out_1, demultiplexer_4_out_0}),
    .in_2(bitextender_7_out), .in_3(bitextender_7_out), .out(d_msk));
  and and_6 (en_str, ucode_d[8], en);
  and and_7 (en_mar, ucode_d[9], en);
  and and_8 (en_ir, ucode_d[10], en);
  Multiplexer multiplexer_20 (.sel(mux_sub), .in_0(ucode_d[11]), .in_1(alt), .out(sub));
  Demultiplexer demultiplexer_5 (.sel(comparator_5_eq), .in(comparator_6_eq), .out_0(fail), .out_1(pass));
  Multiplexer multiplexer_21 (.sel(alt), .in_0(1'b0), .in_1(LN), .out(rs));
  Multiplexer #(.Selector_Bits(3)) multiplexer_22 (
    .sel(funct3), .in_0(Z), .in_1(not_3_out), .in_2(1'b0), .in_3(1'b0), .in_4(lt), .in_5(not_4_out),
    .in_6(ltu), .in_7(not_5_out), .out(multiplexer_22_out));
  Register register_4 (.D(multiplexer_22_out), .C(clk), .en(en), .Q(J));
  BlockRAMDualPort #(.AddrBits(8), .Bits(8)) dat0 (
    .A(d_adr[9:2]), .Din(d_wdat[7:0]), .str(d_msk[0]), .C(clk), .D(dat0_d));
  BlockRAMDualPort #(.AddrBits(8), .Bits(8)) dat1 (
    .A(d_adr[9:2]), .Din(d_wdat[15:8]), .str(d_msk[1]), .C(clk), .D(dat1_d));
  BlockRAMDualPort #(.AddrBits(8), .Bits(8)) dat2 (
    .A(d_adr[9:2]), .Din(d_wdat[23:16]), .str(d_msk[2]), .C(clk), .D(dat2_d));
  BlockRAMDualPort #(.AddrBits(8), .Bits(8)) dat3 (
    .A(d_adr[9:2]), .Din(d_wdat[31:24]), .str(d_msk[3]), .C(clk), .D(dat3_d));

  // Other names for the same wires on the sheet: funct7[5] = alt; busy_t = busy; C = clk; algn[1:0] = d_adr[1:0];
  //   en_t = en

  // Notes on the sheet:
  //   en: default 1
  //   contents of prog (hex, n*v repeats v):
  //   200193,93,113,208733,393,4c771663,300193,100093,100113,208733
  //   ,200393,4a771a63,400193,300093,700113,208733,a00393,48771e63,500193
  //   ,93,ffff8137,208733,ffff83b7,48771263,600193,800000b7,113,208733
  //   ,800003b7,46771663,700193,800000b7,ffff8137,208733,7fff83b7,44771a63
  //   ,800193,93,8137,fff10113,208733,83b7,fff38393,42771a63,900193
  //   ,800000b7,fff08093,113,208733,800003b7,fff38393,40771a63,a00193
  //   ,800000b7,fff08093,8137,fff10113,208733,800083b7,ffe38393,3e771863
  //   ,b00193,800000b7,8137,fff10113,208733,800083b7,fff38393,3c771863
  //   ,c00193,800000b7,fff08093,ffff8137,208733,7fff83b7,fff38393,3a771863
  //   ,d00193,93,fff00113,208733,fff00393,38771c63,e00193,fff00093,100113
  //   ,208733,393,38771063,f00193,fff00093,fff00113,208733,ffe00393
  //   ,36771463,1000193,100093,80000137,fff10113,208733,800003b7,34771663
  //   ,1100193,d00093,b00113,2080b3,1800393,32709a63,1200193,e00093
  //   ,b00113,208133,1900393,30711e63,1300193,d00093,1080b3,1a00393
  //   ,30709463,1400193,213,d00093,b00113,208733,70313,120213,200293
  //   ,fe5214e3,1800393,2c731e63,1500193,213,e00093,b00113,208733,13
  //   ,70313,120213,200293,fe5212e3,1900393,2a731663,1600193,213,f00093
  //   ,b00113,208733,13,13,70313,120213,200293,fe5210e3,1a00393,26731c63
  //   ,1700193,213,d00093,b00113,208733,120213,200293,fe5216e3,1800393
  //   ,24771863,1800193,213,e00093,b00113,13,208733,120213,200293,fe5214e3
  //   ,1900393,22771263,1900193,213,f00093,b00113,13,13,208733,120213
  //   ,200293,fe5212e3,1a00393,1e771a63,1a00193,213,d00093,13,b00113
  //   ,208733,120213,200293,fe5214e3,1800393,1c771463,1b00193,213,e00093
  //   ,13,b00113,13,208733,120213,200293,fe5212e3,1900393,18771c63,1c00193
  //   ,213,f00093,13,13,b00113,208733,120213,200293,fe5212e3,1a00393
  //   ,16771463,1d00193,213,b00113,d00093,208733,120213,200293,fe5216e3
  //   ,1800393,14771063,1e00193,213,b00113,e00093,13,208733,120213,200293
  //   ,fe5214e3,1900393,10771a63,1f00193,213,b00113,f00093,13,13,208733
  //   ,120213,200293,fe5212e3,1a00393,e771263,2000193,213,b00113,13
  //   ,d00093,208733,120213,200293,fe5214e3,1800393,a771c63,2100193
  //   ,213,b00113,13,e00093,13,208733,120213,200293,fe5212e3,1900393
  //   ,8771463,2200193,213,b00113,13,13,f00093,208733,120213,200293
  //   ,fe5212e3,1a00393,4771c63,2300193,f00093,100133,f00393,4711263
  //   ,2400193,2000093,8133,2000393,2711863,2500193,b3,393,2709063,2600193
  //   ,1000093,1e00113,208033,393,701463,2301063,ff0000f,18063,119193
  //   ,11e193,5d00893,18513,73,ff0000f,100193,5d00893,513,73,c0001073
  //   contents of ucode (hex, n*v repeats v):
  //   402,0,0,0,4074c2
endmodule
